# Fritzing sketch rail_system_circuit (saved by Fritzing 0.9.3b)
breadboards: 3

parts:
  Raspberry_Pi_1 = Raspberry Pi 3 [part_number=RPI-3-V1.2]
  Y_Axis_motor_1 = Stepper Motor - Bipolar
  Y_Axis_motor_2 = Stepper Motor - Bipolar
  Pololu_A1 = Pololu A4988 [package=SO16]
  Pololu_A2 = Pololu A4988 [package=SO16]
  J1 = Power Jack [package=power_jack_slot]
  X_Axis_motor = Stepper Motor - Bipolar

nets:
  VDD: Raspberry_Pi_1.3v3, Pololu_A1.VDD, Pololu_A2.VDD
  N1: Raspberry_Pi_1.GPIO5, Pololu_A1.STEP
  N2: Raspberry_Pi_1.GPIO6, Pololu_A1.DIR
  N3: Raspberry_Pi_1.GND, Pololu_A1.GND#8, Pololu_A2.GND#8
  N4: Raspberry_Pi_1.GPIO21, Pololu_A2.STEP
  N5: Raspberry_Pi_1.GPIO20, Pololu_A2.DIR
  N6: Raspberry_Pi_1.GPIO18, Pololu_A1.MS3, Pololu_A2.MS3
  N7: Raspberry_Pi_1.GPIO15, Pololu_A1.MS2, Pololu_A2.MS2
  N8: Raspberry_Pi_1.GPIO14, Pololu_A1.MS1, Pololu_A2.MS1
  N9: Y_Axis_motor_1.A, Y_Axis_motor_2.A, Pololu_A2.2B
  N10: Y_Axis_motor_1.C, Y_Axis_motor_2.C, Pololu_A2.2A
  N11: Y_Axis_motor_1.B, Y_Axis_motor_2.B, Pololu_A2.1A
  N12: Y_Axis_motor_1.D, Y_Axis_motor_2.D, Pololu_A2.1B
  N13: Pololu_A1.RESET, Pololu_A1.SLEEP
  N14: Pololu_A1.1B, X_Axis_motor.D
  N15: Pololu_A1.1A, X_Axis_motor.B
  N16: Pololu_A1.2A, X_Axis_motor.C
  N17: Pololu_A1.2B, X_Axis_motor.A
  N18: Pololu_A1.GND#14, Pololu_A2.GND#14, J1.GNDBREAK
  N19: Pololu_A1.VMOT, Pololu_A2.VMOT, J1.GND
  N20: Pololu_A2.RESET, Pololu_A2.SLEEP
